// Digital circuit main.dig as structural Verilog
module main (
);

  wire undriven_4;
  wire [1:0] undriven_3;
  wire [7:0] eepromdualport_1_d, eepromdualport_2_d;
  wire [15:0] undriven, undriven_2;

  EEPROMDualPort eepromdualport_1 (.A(undriven_3), .Din(undriven_4), .D(eepromdualport_1_d[0]));  // open: str, C, ld
  EEPROMDualPort eepromdualport_2 (.A(undriven_3), .Din(undriven_4), .D(eepromdualport_2_d[0]));  // open: str, C, ld
  REG_A reg_a_1 ();  // open: AI, AO, BUS_i, BUS_o
  ALU alu_1 (.A(undriven), .B(undriven_2));  // open: C_i, Op
  REG_B reg_b_1 ();  // open: BUS_i, BUS_o, BI, BO
  // Pins of 1 and 8 bits meet at eepromdualport_1_d
  // Pins of 1 and 8 bits meet at eepromdualport_2_d
endmodule
